// Logisim project address_decode.circ as structural Verilog: 1 circuit, main circuit main
module main (
);

  wire A0, A1, A2, A3, A4, A5, A6, A7, A8, A9, A10, A11, A12, A13, A13OR12, A14, A15, and_1_out, and_2_out,
       and_3_out, and_4_out, and_6_out, and_7_out, and_8_out, and_9_out, and_10_out, and_11_out, and_12_out,
       and_13_out, and_14_out, and_15_out, B1, B2, BB, BSS, C006, C007, C030, CLK, CS_CPUBUS, CS_DEVICE,
       CS_RAM, CS_ROM, CXXX, decoder_1_out0, decoder_1_out3, decoder_1_out5, decoder_1_out6, decoder_1_out8,
       decoder_2_out0, decoder_2_out1, decoder_2_out2, decoder_2_out3, decoder_2_out4, decoder_2_out5,
       decoder_2_out6, decoder_2_out7, decoder_2_out8, decoder_2_out9, decoder_2_out10, decoder_2_out11,
       decoder_2_out12, decoder_2_out13, decoder_2_out14, decoder_2_out15, DEV, DXXX, FF, FULLMODE, GFXMODE,
       GFXSS, HIRES, JOYSS, KBD, LORES, LOW0, MIXMODE, nand_3_out, nand_5_out, nand_6_out, nand_7_out,
       nand_8_out, nand_9_out, nand_10_out, nand_16_out, nand_18_out, nand_23_out, not_1_out, not_2_out,
       not_24_out, not_25_out, not_26_out, not_27_out, not_28_out, not_29_out, not_30_out, not_31_out,
       not_32_out, not_33_out, NOWRITE, OE, or_1_out, or_2_out, or_9_out, or_12_out, or_15_out, or_17_out,
       or_18_out, or_19_out, or_20_out, or_21_out, or_22_out, or_23_out, or_24_out, or_25_out, or_26_out,
       or_27_out, or_28_out, or_29_out, or_30_out, or_31_out, or_33_out, or_34_out, PAGE1, PAGE2, PHI2, RAM,
       RAMREAD, RAMWRITE, ROM, ROMREAD, RW, SS, TXTMODE, VIDBUS, VIDENABLE, WE, x0, x00, x000, x1, x2, x3,
       x4, x5, x6, x7, x8, x9, x30, x50, x60, x80, xA, xB;

  not not_1 (not_1_out, A13);
  not not_2 (not_2_out, A12);
  or or_1 (or_1_out, A11, A10);
  or or_2 (or_2_out, A9, A8);
  or or_3 (LOW0, x00, x0);
  and and_1 (and_1_out, A15, A14);
  and and_2 (and_2_out, not_2_out, not_1_out);
  and and_3 (and_3_out, not_1_out, A12);
  or or_4 (x000, or_1_out, or_2_out);
  Decoder #(.select(4)) decoder_1 (
    .out0(decoder_1_out0), .out3(decoder_1_out3), .out5(decoder_1_out5), .out6(decoder_1_out6),
    .out8(decoder_1_out8), .sel({A7, A6, A5, A4}));  // open: out1, out2, out4, out7, out9, out10, out11, out12, out13, out14, out15, en
  not not_3 (x00, decoder_1_out0);
  not not_4 (x30, decoder_1_out3);
  not not_5 (x50, decoder_1_out5);
  not not_6 (x60, decoder_1_out6);
  Decoder #(.select(4)) decoder_2 (
    .out0(decoder_2_out0), .out1(decoder_2_out1), .out2(decoder_2_out2), .out3(decoder_2_out3),
    .out4(decoder_2_out4), .out5(decoder_2_out5), .out6(decoder_2_out6), .out7(decoder_2_out7),
    .out8(decoder_2_out8), .out9(decoder_2_out9), .out10(decoder_2_out10), .out11(decoder_2_out11),
    .out12(decoder_2_out12), .out13(decoder_2_out13), .out14(decoder_2_out14), .out15(decoder_2_out15),
    .sel({A3, A2, A1, A0}));  // open: en
  not not_7 (x0, decoder_2_out0);
  not not_8 (x1, decoder_2_out1);
  not not_9 (x2, decoder_2_out2);
  not not_10 (x3, decoder_2_out3);
  not not_11 (x4, decoder_2_out4);
  not not_12 (x5, decoder_2_out5);
  not not_13 (x6, decoder_2_out6);
  or or_5 (SS, CXXX, x000);
  Hex_Digit_Display hex_digit_display_1 (.value({A15, A14, A13, A12}));  // open: dp
  DipSwitch #(.number(16)) dipswitch_1 (
    .sw1(A15), .sw2(A14), .sw3(A13), .sw4(A12), .sw5(A11), .sw6(A10), .sw7(A9), .sw8(A8), .sw9(A7),
    .sw10(A6), .sw11(A5), .sw12(A4), .sw13(A3), .sw14(A2), .sw15(A1), .sw16(A0));
  nand nand_1 (CXXX, and_1_out, and_2_out);
  not not_14 (x80, decoder_1_out8);
  not not_15 (x7, decoder_2_out7);
  not not_16 (x8, decoder_2_out8);
  not not_17 (x9, decoder_2_out9);
  not not_18 (xA, decoder_2_out10);
  not not_19 (xB, decoder_2_out11);
  // NOT_Gate not_20 has open pins: in=decoder_2_out12, out=open
  // NOT_Gate not_21 has open pins: in=decoder_2_out13, out=open
  // NOT_Gate not_22 has open pins: in=decoder_2_out14, out=open
  or or_6 (C007, x7, or_9_out);
  Hex_Digit_Display hex_digit_display_2 (.value({A11, A10, A9, A8}));  // open: dp
  Hex_Digit_Display hex_digit_display_3 (.value({A7, A6, A5, A4}));  // open: dp
  // NOT_Gate not_23 has open pins: in=decoder_2_out15, out=open
  or or_7 (GFXSS, SS, x50);
  or or_8 (C006, or_9_out, x6);
  or or_9 (or_9_out, SS, x00);
  Hex_Digit_Display hex_digit_display_4 (.value({A3, A2, A1, A0}));  // open: dp
  nand nand_2 (DXXX, and_1_out, and_3_out);
  Clock clock_1 (.out(CLK));
  or or_10 (BSS, SS, x80);
  or or_11 (C030, x0, or_12_out);
  or or_12 (or_12_out, SS, x30);
  nand nand_3 (nand_3_out, JOYSS, KBD);
  or or_13 (JOYSS, SS, x60);
  LED u_dev (.in(DEV));
  or or_14 (DEV, nand_3_out, or_15_out);
  or or_15 (or_15_out, nand_5_out, or_17_out);
  or or_16 (A13OR12, A13, A12);
  or or_17 (or_17_out, A13OR12, A11);
  LED u_ram (.in(RAM));
  nand nand_4 (RAM, DEV, ROM);
  nand nand_5 (nand_5_out, A14, A15);
  and and_4 (and_4_out, x2, xA);
  LED u_rom (.in(ROM));
  and and_5 (ROM, or_18_out, nand_7_out);
  or or_18 (or_18_out, or_19_out, or_23_out);
  or or_19 (or_19_out, nand_5_out, and_6_out);
  and and_6 (and_6_out, not_24_out, not_26_out);
  not not_24 (not_24_out, A12);
  nand nand_6 (nand_6_out, or_20_out, or_24_out);
  or or_20 (or_20_out, and_4_out, BSS);
  nand nand_7 (nand_7_out, and_7_out, not_25_out);
  and and_7 (and_7_out, and_8_out, BB);
  and and_8 (and_8_out, A13OR12, A15);
  or or_21 (or_21_out, nand_8_out, nand_9_out);
  nand nand_8 (nand_8_out, or_20_out, or_22_out);
  or or_22 (or_22_out, and_9_out, BSS);
  and and_9 (and_9_out, x1, x9);
  not not_25 (not_25_out, A14);
  or or_23 (or_23_out, and_10_out, and_13_out);
  and and_10 (and_10_out, RAMREAD, RW);
  not not_26 (not_26_out, A13);
  LED A16 (.in(and_11_out));
  and and_11 (and_11_out, and_12_out, not_27_out);
  and and_12 (and_12_out, or_23_out, B2);
  and and_13 (and_13_out, RAMWRITE, not_28_out);
  J_K_Flip_Flop j_k_ff_1 (
    .J(FF), .K(NOWRITE), .clk(or_21_out), .Q(RAMWRITE), .Qn(NOWRITE), .reset(nand_6_out));  // open: preset
  nand nand_9 (nand_9_out, or_24_out, or_25_out);
  or or_24 (or_24_out, and_14_out, BSS);
  and and_14 (and_14_out, x8, x0);
  not not_27 (not_27_out, DXXX);
  not not_28 (not_28_out, RW);
  J_K_Flip_Flop j_k_ff_2 (.J(nand_8_out), .K(nand_9_out), .clk(CLK), .Q(ROMREAD), .Qn(RAMREAD));  // open: preset, reset
  nand nand_10 (nand_10_out, or_22_out, or_25_out);
  J_K_Flip_Flop j_k_ff_3 (.J(nand_10_out), .K(1'b0), .clk(CLK), .Q(FF), .reset(nand_6_out));  // open: Qn, preset
  or or_25 (or_25_out, and_15_out, BSS);
  and and_15 (and_15_out, xB, x3);
  LED GFX (.in(or_26_out));
  or or_26 (or_26_out, GFXSS, x0);
  nand nand_11 (PAGE1, or_27_out, PAGE2);
  LED u_PAGE1 (.in(or_27_out));
  or or_27 (or_27_out, GFXSS, x4);
  nand nand_12 (BB, C007, nand_16_out);
  nand nand_13 (GFXMODE, or_26_out, TXTMODE);
  LED TXT (.in(or_28_out));
  or or_28 (or_28_out, GFXSS, x1);
  nand nand_14 (PAGE2, PAGE1, or_29_out);
  nand nand_15 (TXTMODE, GFXMODE, or_28_out);
  LED u_PAGE2 (.in(or_29_out));
  or or_29 (or_29_out, GFXSS, x5);
  nand nand_16 (nand_16_out, BB, C006);
  nand nand_17 (B1, nand_18_out, B2);
  nand nand_18 (nand_18_out, not_29_out, A3);
  not not_29 (not_29_out, BSS);
  LED FULL (.in(or_30_out));
  or or_30 (or_30_out, GFXSS, x2);
  nand nand_19 (LORES, or_31_out, HIRES);
  LED u_LORES (.in(or_31_out));
  or or_31 (or_31_out, GFXSS, x6);
  LED u_KBD (.in(KBD));
  or or_32 (KBD, SS, LOW0);
  nand nand_20 (B2, B1, nand_23_out);
  not not_30 (not_30_out, A3);
  nand nand_21 (FULLMODE, or_30_out, MIXMODE);
  LED MIX (.in(or_33_out));
  or or_33 (or_33_out, GFXSS, x3);
  nand nand_22 (HIRES, LORES, or_34_out);
  nand nand_23 (nand_23_out, not_30_out, not_29_out);
  nand nand_24 (MIXMODE, FULLMODE, or_33_out);
  LED u_HIRES (.in(or_34_out));
  or or_34 (or_34_out, GFXSS, x7);
  not not_31 (not_31_out, VIDENABLE);
  DipSwitch #(.number(5)) dipswitch_2 (.sw1(PHI2), .sw2(VIDENABLE), .sw3(VIDBUS), .sw5(RW));  // open: sw4
  not not_32 (not_32_out, RW);
  not not_33 (not_33_out, PHI2);
  or or_35 (CS_ROM, not_31_out, ROM);
  or or_36 (CS_DEVICE, not_31_out, DEV);
  or or_37 (CS_CPUBUS, not_31_out, RAM);
  and and_16 (CS_RAM, RAM, VIDBUS);
  and and_17 (OE, VIDBUS, not_32_out);
  or or_38 (WE, RW, not_33_out);
endmodule
